// Logisim project s-mips.circ as structural Verilog: 17 circuits, main circuit S-MIPS Board
module S_MIPS_Board (
  input  DESHABILITAR_DISPATCHER,
  output halt
);

  wire button_1_out, CLK, CS, d_ff_1_q, LCLR, LoadRAM, LoadRAMOn, LW, R_R_W, R_W, ram_dispatcher_1_finished,
       RCS, Reset_out, RST, TTY_EN;
  wire [2:0] KDB;
  wire [3:0] LMask, Mask, ram_1_read_time, ram_1_write_time, RMask;
  wire [6:0] KDB_DATA, TTY_DATA;
  wire [15:0] Addr, LAddr, RAddr;
  wire [31:0] I0, I1, I2, I3, LData, ram_1_data_out_0, ram_1_data_out_1, ram_1_data_out_2, ram_1_data_out_3,
       RI0, RI1, RI2, RI3;

  TTY #(.rows(25), .cols(80)) tty_1 (.data(TTY_DATA), .clk(CLK), .we(TTY_EN), .clr(RST));
  not not_1 (LoadRAMOn, ram_dispatcher_1_finished);
  RAM_Dispatcher ram_dispatcher_1 (
    .WriteTime(ram_1_write_time), .Clock(CLK), .Data(LData), .Address(LAddr), .Mask(LMask),
    .Finished(ram_dispatcher_1_finished), .Write(LW), .CLR(LCLR));
  Keyboard #(.buflen(64)) keyboard_1 (.clk(CLK), .re(KDB[0]), .avail(KDB[2]), .data(KDB_DATA));  // open: clr
  RAM ram_1 (
    .Address(RAddr), .Data_Out_0(ram_1_data_out_0), .Data_Out_1(ram_1_data_out_1),
    .Data_Out_2(ram_1_data_out_2), .Data_Out_3(ram_1_data_out_3), .Data_In_0(RI0), .Data_In_1(RI1),
    .Data_In_2(RI2), .Data_In_3(RI3), .Mask(RMask), .nRead_Write(R_R_W), .Chip_Select(RCS),
    .Read_Time(ram_1_read_time), .Reset(button_1_out), .Write_Time(ram_1_write_time));
  Button button_1 (.out(button_1_out));
  D_Flip_Flop d_ff_1 (.clk(CLK), .D(1'b1), .Q(d_ff_1_q), .reset(Reset_out));  // open: Qn, preset, en
  Button Reset (.out(Reset_out));
  S_MIPS s_mips_1 (
    .Kbd_Enable(KDB[0]), .Address(Addr), .Kbd_Clear(KDB[1]), .Kbd_Available(KDB[2]), .RAM_In_0(I0),
    .Kbd_ASCII_Data(KDB_DATA), .RAM_In_1(I1), .TTY_Enable(TTY_EN), .RAM_In_2(I2), .RAM_In_3(I3),
    .TTY_ASCII_Data(TTY_DATA), .RAM_Out_0(ram_1_data_out_0), .RAM_Out_1(ram_1_data_out_1), .out_19(halt),
    .RAM_Out_2(ram_1_data_out_2), .RAM_Out_3(ram_1_data_out_3), .Mask(Mask), .Read_Time(ram_1_read_time),
    .Write_Time(ram_1_write_time), .nRead_Write(R_W), .Chip_Select(CS), .Reset(RST), .Clock(CLK));
  D_Flip_Flop d_ff_2 (.clk(CLK), .D(d_ff_1_q), .Qn(LCLR), .reset(Reset_out));  // open: Q, preset, en
  or or_1 (RST, LCLR, LoadRAM);
  Clock clock_1 (.out(CLK));
  Multiplexer #(.width(32), .enable("false")) multiplexer_1 (.in0(I0), .in1(LData), .out(RI0), .sel(LoadRAM));
  Multiplexer #(.width(32), .enable("false")) multiplexer_2 (.in0(I1), .in1(LData), .out(RI1), .sel(LoadRAM));
  Multiplexer #(.width(32), .enable("false")) multiplexer_3 (.in0(I2), .in1(LData), .out(RI2), .sel(LoadRAM));
  Multiplexer #(.width(32), .enable("false")) multiplexer_4 (.in0(I3), .in1(LData), .out(RI3), .sel(LoadRAM));
  and and_1 (LoadRAM, ~DESHABILITAR_DISPATCHER, LoadRAMOn);  // AND_Gate
  Multiplexer #(.width(16), .enable("false")) multiplexer_5 (.in0(Addr), .in1(LAddr), .out(RAddr), .sel(LoadRAM));
  Multiplexer #(.width(4), .enable("false")) multiplexer_6 (.in0(Mask), .in1(LMask), .out(RMask), .sel(LoadRAM));
  Multiplexer #(.enable("false")) multiplexer_7 (.in0(CS), .in1(LW), .out(RCS), .sel(LoadRAM));
  Multiplexer #(.enable("false")) multiplexer_8 (.in0(R_W), .in1(LW), .out(R_R_W), .sel(LoadRAM));

  // Notes on the sheet:
  //   NO MODIFICAR
  //   Keyboard
endmodule

module RAM (
  input  [15:0] Address,
  input  [31:0] Data_In_0,
  input  [31:0] Data_In_1,
  input  [31:0] Data_In_2,
  input  [31:0] Data_In_3,
  input  [3:0] Mask,
  input  nRead_Write,
  input  Chip_Select,
  input  Reset,
  output [31:0] Data_Out_0,
  output [31:0] Data_Out_1,
  output [31:0] Data_Out_2,
  output [31:0] Data_Out_3,
  output [3:0] Read_Time,
  output [3:0] Write_Time
);

  wire and_2_out, and_3_out, and_4_out, and_5_out, and_6_out, and_7_out, and_8_out, and_9_out, Changed, CLK,
       comparator_2_eq, comparator_3_eq, comparator_4_eq, comparator_5_eq, comparator_6_eq, Count,
       demultiplexer_3_out0, Idle, Idle_q, Load, Load0, Load1, nand_1_out, or_1_out, or_2_out, or_3_out,
       or_4_out, or_5_out, or_6_out, or_7_out, or_8_out, or_9_out, or_10_out, Proc_q, Update_Mem, Zero_Time;
  wire [3:0] counter_1_q, multiplexer_1_out, subtractor_1_out;
  wire [31:0] register_1_q, register_2_q, register_3_q, register_4_q, register_5_q;

  // Probe on 4'b0011
  // Probe on 4'b0010
  Multiplexer #(.width(4), .enable("false")) multiplexer_1 (
    .in0(4'b0011), .in1(4'b0010), .out(multiplexer_1_out), .sel(nRead_Write));
  or or_1 (or_1_out, Idle, Update_Mem);
  or or_2 (or_2_out, ~Chip_Select, Reset);  // OR_Gate
  Subtractor #(.width(4)) subtractor_1 (.a(multiplexer_1_out), .b(4'b0010), .out(subtractor_1_out));  // open: bin, bout
  D_Flip_Flop u_Idle (.clk(CLK), .D(or_1_out), .Q(Idle_q), .preset(or_2_out));  // open: Qn, en, reset
  Demultiplexer #(.enable("false")) demultiplexer_1 (.out0(Idle), .out1(Load0), .in(Idle_q), .sel(Changed));
  // Probe on counter_1_q
  Counter #(.width(4), .max('hf)) counter_1 (
    .load(Load), .D(subtractor_1_out), .count(Count), .Q(counter_1_q), .clk(CLK), .clr(or_3_out));  // open: carry
  or or_3 (or_3_out, ~Chip_Select, Reset);  // OR_Gate
  Comparator #(.width(4), .mode("unsigned")) comparator_1 (
    .a(4'b0000), .b(counter_1_q), .eq(Zero_Time));  // open: gt, lt
  or or_4 (or_4_out, Count, Load0, Load1);
  Register #(.width(32)) register_1 (.D(Data_In_0), .en(Chip_Select), .Q(register_1_q), .clk(CLK), .clr(or_5_out));
  or or_5 (or_5_out, ~Chip_Select, Reset);  // OR_Gate
  Register #(.width(32)) register_2 (.D(Data_In_1), .en(Chip_Select), .Q(register_2_q), .clk(CLK), .clr(or_6_out));
  or or_6 (or_6_out, ~Chip_Select, Reset);  // OR_Gate
  Register #(.width(32)) register_3 (.D(Data_In_2), .en(Chip_Select), .Q(register_3_q), .clk(CLK), .clr(or_7_out));
  or or_7 (or_7_out, ~Chip_Select, Reset);  // OR_Gate
  Register #(.width(32)) register_4 (.D(Data_In_3), .en(Chip_Select), .Q(register_4_q), .clk(CLK), .clr(or_8_out));
  or or_8 (or_8_out, ~Chip_Select, Reset);  // OR_Gate
  Register #(.width(32)) register_5 (
    .D({{11{1'b1}}, nRead_Write, Mask, Address}), .en(Chip_Select), .Q(register_5_q), .clk(CLK),
    .clr(or_9_out));
  or or_9 (or_9_out, ~Chip_Select, Reset);  // OR_Gate
  D_Flip_Flop Proc (.clk(CLK), .D(or_4_out), .Q(Proc_q), .reset(or_10_out));  // open: Qn, preset, en
  or or_10 (or_10_out, ~Chip_Select, Reset);  // OR_Gate
  Demultiplexer #(.enable("false")) demultiplexer_2 (
    .out0(Count), .out1(Update_Mem), .in(demultiplexer_3_out0), .sel(Zero_Time));
  Demultiplexer #(.enable("false")) demultiplexer_3 (
    .out0(demultiplexer_3_out0), .out1(Load1), .in(Proc_q), .sel(Changed));
  Clock clock_1 (.out(CLK));
  Comparator #(.width(32)) comparator_2 (.a(register_1_q), .b(Data_In_0), .eq(comparator_2_eq));  // open: gt, lt
  Comparator #(.width(32)) comparator_3 (.a(register_2_q), .b(Data_In_1), .eq(comparator_3_eq));  // open: gt, lt
  Comparator #(.width(32)) comparator_4 (.a(register_3_q), .b(Data_In_2), .eq(comparator_4_eq));  // open: gt, lt
  Comparator #(.width(32)) comparator_5 (.a(register_4_q), .b(Data_In_3), .eq(comparator_5_eq));  // open: gt, lt
  Comparator #(.width(32)) comparator_6 (
    .a(register_5_q), .b({{11{1'b1}}, nRead_Write, Mask, Address}), .eq(comparator_6_eq));  // open: gt, lt
  nand nand_1 (nand_1_out, comparator_6_eq, comparator_2_eq, comparator_3_eq, comparator_4_eq, comparator_5_eq);
  and and_1 (Changed, nand_1_out, Chip_Select);
  or or_11 (Load, Count, Load1, Load0);
  and and_2 (and_2_out, Mask[0], Update_Mem, nRead_Write);
  and and_3 (and_3_out, Mask[1], Update_Mem, nRead_Write);
  and and_4 (and_4_out, Mask[2], Update_Mem, nRead_Write);
  and and_5 (and_5_out, Mask[3], Update_Mem, nRead_Write);
  RAM_part #(.addrWidth(16), .dataWidth(32), .bus("separate")) ram_1 (
    .addr(Address), .din(Data_In_0), .data(Data_Out_0), .str(and_2_out), .sel(Chip_Select), .clk(CLK),
    .ld(and_6_out), .clr(Reset));
  and and_6 (and_6_out, ~nRead_Write, Idle);  // AND_Gate
  RAM_part #(.addrWidth(16), .dataWidth(32), .bus("separate")) ram_2 (
    .addr(Address), .din(Data_In_1), .data(Data_Out_1), .str(and_3_out), .sel(Chip_Select), .clk(CLK),
    .ld(and_7_out), .clr(Reset));
  and and_7 (and_7_out, ~nRead_Write, Idle);  // AND_Gate
  RAM_part #(.addrWidth(16), .dataWidth(32), .bus("separate")) ram_3 (
    .addr(Address), .din(Data_In_2), .data(Data_Out_2), .str(and_4_out), .sel(Chip_Select), .clk(CLK),
    .ld(and_8_out), .clr(Reset));
  and and_8 (and_8_out, ~nRead_Write, Idle);  // AND_Gate
  RAM_part #(.addrWidth(16), .dataWidth(32), .bus("separate")) ram_4 (
    .addr(Address), .din(Data_In_3), .data(Data_Out_3), .str(and_5_out), .sel(Chip_Select), .clk(CLK),
    .ld(and_9_out), .clr(Reset));
  and and_9 (and_9_out, ~nRead_Write, Idle);  // AND_Gate

  assign Read_Time = 4'b0011;
  assign Write_Time = 4'b0010;

  // Other names for the same wires on the sheet: M0 = Mask[0]; M1 = Mask[1]; M2 = Mask[2]; M3 = Mask[3];
  //   RW = nRead_Write; CLR = Reset; CS = Chip_Select; Load2 = Count

  // Notes on the sheet:
  //   NO MODIFICAR
  //   excepto quizás los valores RT y WT
  //   BANK0
  //   BANK1
  //   BANK2
  //   BANK3
endmodule

module S_MIPS (
  input  [3:0] Read_Time,
  input  [31:0] RAM_Out_0,
  input  [3:0] Write_Time,
  input  Kbd_Available,
  input  [31:0] RAM_Out_1,
  input  [6:0] Kbd_ASCII_Data,
  input  [31:0] RAM_Out_2,
  input  Reset,
  input  Clock,
  input  [31:0] RAM_Out_3,
  output [15:0] Address,
  output [31:0] RAM_In_0,
  output [3:0] Mask,
  output [31:0] RAM_In_1,
  output Kbd_Enable,
  output Kbd_Clear,
  output [31:0] RAM_In_2,
  output TTY_Enable,
  output out_19,
  output [6:0] TTY_ASCII_Data,
  output [31:0] RAM_In_3,
  output nRead_Write,
  output Chip_Select
);

  wire DA_S, E_Cache, End_RAM, Hit, Load_inst, Logical_Op, PC_Enable, pop, push, push_I, R_I, R_W, Read,
       Write;
  wire [1:0] ALU_SB, Bank, S_Adress;
  wire [2:0] Branch_Op, DATA_S;
  wire [3:0] ALU_Op;
  wire [5:0] Func_Code, Op_Code;
  wire [31:0] Adress, Cache_Out, DATA_IN, RAM_Data, RAM_Write, Value;

  Control_Unit control_unit_1 (
    .in_1(Op_Code), .in_2(Read_Time), .in_3(Clock), .in_5(Func_Code), .in_6(Write_Time), .out_16(out_19),
    .out_9(ALU_Op), .out_10(Kbd_Enable), .out_11(Load_inst), .out_12(DATA_S), .out_13(push_I),
    .Salidas(TTY_Enable), .out_17(pop), .out_19(push), .out_21(PC_Enable), .out_23(Logical_Op),
    .out_24(DA_S), .out_25(S_Adress), .out_26(Branch_Op), .out_27(ALU_SB), .out_29(Chip_Select),
    .out_30(R_W), .in_4(Hit), .out_15(E_Cache), .out_22(Read), .out_18(Write), .Write_RAM(nRead_Write),
    .in_7(Reset), .out_28(R_I), .out_8(End_RAM));
  RAM_Manager ram_manager_1 (
    .in_1(RAM_Out_0), .in_2(RAM_Out_1), .in_3(Adress), .in_8(Clock), .in_9(Reset), .in_6(RAM_Out_2),
    .in_7(RAM_Out_3), .out_10(Address), .Salidas(Mask), .out_12(RAM_Data), .out_13(Bank), .in_5(Hit),
    .out_14(RAM_In_0), .out_15(RAM_In_1), .out_16(RAM_In_2), .out_17(RAM_In_3), .in_4(RAM_Write));
  Data_Path data_path_1 (
    .in_1(R_W), .in_2(DA_S), .in_3(DATA_S), .in_4(Logical_Op), .in_5(S_Adress), .in_6(ALU_Op), .in_8(ALU_SB),
    .in_9(Branch_Op), .in_12(PC_Enable), .in_13(DATA_IN), .in_14(Load_inst), .in_15(Kbd_ASCII_Data),
    .in_16(Kbd_Available), .in_17(Reset), .in_20(Clock), .out_21(Op_Code), .out_22(Adress), .out_23(Value),
    .out_24(Func_Code), .out_25(TTY_ASCII_Data), .in_18(pop), .in_19(push), .in_10(push_I), .in_7(R_I),
    .in_11(End_RAM));
  Multiplexer #(.width(32), .enable("false")) multiplexer_1 (.in0(RAM_Data), .in1(Cache_Out), .out(DATA_IN), .sel(Hit));
  Cache cache_1 (
    .in_1(Clock), .in_3(Reset), .in_6(Write), .in_7(Value), .out_13(Cache_Out), .in_5(Read),
    .in_8(RAM_Out_0), .in_9(RAM_Out_1), .in_10(RAM_Out_2), .in_11(RAM_Out_3), .in_4(Adress), .in_2(E_Cache),
    .out_14(RAM_Write), .out_12(Hit));
  // Probe on nothing

  assign Kbd_Clear = Reset;

  // Other names for the same wires on the sheet: CLK = Clock; CS = Chip_Select; KBD_AVAIL = Kbd_Available;
  //   CLR = Reset; KBD_CLR = Reset; KBD_DATA[6:0] = Kbd_ASCII_Data; RAM_A[15:0] = Address;
  //   RAM_INPUT_0[31:0] = RAM_In_0; RAM_INPUT_1[31:0] = RAM_In_1; RAM_INPUT_2[31:0] = RAM_In_2;
  //   RAM_INPUT_3[31:0] = RAM_In_3; RAM_MASK[3:0] = Mask; RAM_OUTPUT_0[31:0] = RAM_Out_0;
  //   RAM_OUTPUT_1[31:0] = RAM_Out_1; RAM_OUTPUT_2[31:0] = RAM_Out_2; RAM_OUTPUT_3[31:0] = RAM_Out_3; STOP = out_19;
  //   TTY_DATA[6:0] = TTY_ASCII_Data; WRAM = nRead_Write

  // Notes on the sheet:
  //   DATA FROM RAM
  //   Entradas
  //   RAM TIMING
  //   KEYBOARD
  //   SEQUENCING
  //   DATA TO RAM
  //   Salidas
  //   RAM ADDRESS
  //   DATA WRITE MASK
  //   KEYBOARD
  //   TTY
  //   RAM CONTROL
endmodule

module RAM_Dispatcher (
  input  [3:0] WriteTime,
  input  Clock,
  input  CLR,
  output [31:0] Data,
  output [15:0] Address,
  output [3:0] Mask,
  output Finished,
  output Write
);

  wire demultiplexer_2_out1, demultiplexer_3_out1, End, IDLE_q, IncAddr, Load, or_1_out, or_2_out, While_q,
       WriteEnd;
  wire [3:0] counter_1_q;
  wire [31:0] CurrentAddress_q;

  Counter #(.width(32), .max('hffffffff)) CurrentAddress (
    .count(IncAddr), .Q({CurrentAddress_q[31:18], Address, CurrentAddress_q[1:0]}), .clk(Clock), .clr(CLR));  // open: load, D, carry
  or or_1 (or_1_out, IncAddr, demultiplexer_3_out1, Finished);
  D_Flip_Flop IDLE (.clk(Clock), .D(or_1_out), .Q(IDLE_q), .preset(CLR));  // open: Qn, en, reset
  Demultiplexer #(.enable("false")) demultiplexer_1 (.out0(Load), .out1(Finished), .in(IDLE_q), .sel(End));
  D_Flip_Flop While (.clk(Clock), .D(or_2_out), .Q(While_q), .reset(CLR));  // open: Qn, preset, en
  or or_2 (or_2_out, Write, Load);
  RAM_part #(.addrWidth(18), .dataWidth(32)) ram_1 (
    .addr({Address, CurrentAddress_q[1:0]}), .data(Data), .clk(Clock));  // open: sel, ld, clr
  Demultiplexer #(.enable("false")) demultiplexer_2 (
    .out0(Write), .out1(demultiplexer_2_out1), .in(While_q), .sel(WriteEnd));
  Decoder #(.select(2)) decoder_1 (
    .out0(Mask[0]), .out1(Mask[1]), .out2(Mask[2]), .out3(Mask[3]), .sel(CurrentAddress_q[1:0]));  // open: en
  Demultiplexer #(.enable("false")) demultiplexer_3 (
    .out0(IncAddr), .out1(demultiplexer_3_out1), .in(demultiplexer_2_out1), .sel(End));
  Counter #(.width(4), .max('hf)) counter_1 (
    .load(Load), .D(WriteTime), .count(Write), .Q(counter_1_q), .clk(Clock));  // open: carry, clr
  Comparator #(.width(32)) comparator_1 (.a(Data), .b({32{1'b1}}), .eq(End));  // open: gt, lt
  Comparator #(.width(4)) comparator_2 (.a(4'b0000), .b(counter_1_q), .eq(WriteEnd));  // open: gt, lt

  // Other names for the same wires on the sheet: CLK = Clock; Count = Write; WT[3:0] = WriteTime
endmodule

module Control_Unit (
  input  [5:0] in_1,
  input  [3:0] in_2,
  input  in_3,
  input  in_4,
  input  [5:0] in_5,
  input  [3:0] in_6,
  input  in_7,
  output out_8,
  output [3:0] out_9,
  output out_10,
  output out_11,
  output [2:0] out_12,
  output out_13,
  output Salidas,
  output out_15,
  output out_16,
  output out_17,
  output out_18,
  output out_19,
  output Write_RAM,
  output out_21,
  output out_22,
  output out_23,
  output out_24,
  output [1:0] out_25,
  output [2:0] out_26,
  output [1:0] out_27,
  output out_28,
  output out_29,
  output out_30
);

  wire ALU, and_1_out, and_4_out, and_5_out, Brach, cache_q, clok_1, comparator_1_eq, comparator_2_eq,
       comparator_4_eq, CS_0, CS_1, demultiplexer_1_out0, demultiplexer_2_out0, demultiplexer_3_out0,
       demultiplexer_3_out1, demultiplexer_4_out0, demultiplexer_6_out1, demultiplexer_7_out0,
       demultiplexer_7_out1, Especial, Hi_Lo_Op, IDLE_q, Inmediate, lw, NORAM, not_1_out, or_3_out, or_4_out,
       or_5_out, or_6_out, or_7_out, or_9_out, or_10_out, R_W_3, R_W_4, R_W_6, RAM, Save_Instruction_q,
       Stack, stack_q, TTY, Wait;
  wire [1:0] Especial_Op;
  wire [2:0] CU_Op;
  wire [3:0] counter_1_q, multiplexer_1_out, RT_v_WT;

  Operation_Decoder operation_decoder_1 (
    .Entradas(in_1), .in_2(in_5), .Salidas(out_17), .out_6(lw), .out_8(out_24), .out_9(out_27),
    .out_10(CU_Op), .out_11(out_9), .out_12(out_12), .out_13(out_26), .out_14(out_23), .out_15(Especial_Op),
    .out_4(out_22), .out_7(out_18), .out_3(out_19));
  Multiplexer #(.width(4), .enable("false")) multiplexer_1 (
    .in0(in_2), .in1(in_6), .out(multiplexer_1_out), .sel(out_18));
  Multiplexer #(.width(4), .enable("false")) multiplexer_2 (
    .in0(multiplexer_1_out), .in1(in_2), .out(RT_v_WT), .sel(CS_0));
  or or_1 (out_29, CS_0, CS_1);
  and and_1 (and_1_out, ALU, ~Hi_Lo_Op);  // AND_Gate
  Comparator #(.width(3)) comparator_1 (.a(CU_Op), .b(3'b100), .eq(comparator_1_eq));  // open: gt, lt
  Comparator #(.width(3)) comparator_2 (.a(CU_Op), .b(3'b101), .eq(comparator_2_eq));  // open: gt, lt
  or or_2 (out_30, and_1_out, Inmediate, R_W_3, out_10, R_W_6, R_W_4);
  Priority_Encoder #(.select(2), .disabled(0)) priority_encoder_1 (
    .in0(1'b1), .in1(comparator_1_eq), .in2(comparator_2_eq), .out(out_25), .en_in(1'b1));  // open: in3, gs, en_out
  Counter #(.width(4), .max('hf)) counter_1 (
    .Q(counter_1_q), .clk(in_3), .clr(or_3_out));  // open: load, D, count, carry
  or or_3 (or_3_out, clok_1, out_28);
  and and_2 (Hi_Lo_Op, out_9[3], ~out_9[2]);  // AND_Gate
  Comparator #(.width(4)) comparator_3 (.a(RT_v_WT), .b(counter_1_q), .eq(Wait));  // open: gt, lt
  D_Flip_Flop IDLE (.clk(in_3), .D(or_4_out), .Q(IDLE_q), .preset(in_7));  // open: Qn, en, reset
  Demultiplexer #(.enable("false")) demultiplexer_1 (
    .out0(demultiplexer_1_out0), .out1(out_28), .in(IDLE_q), .sel(not_1_out));
  or or_4 (or_4_out, demultiplexer_1_out0, NORAM, out_8);
  Demultiplexer #(.select(2), .enable("false")) demultiplexer_2 (
    .out0(demultiplexer_2_out0), .out1(R_W_6), .out2(out_10), .out3(TTY), .in(Especial), .sel(Especial_Op));
  not not_1 (not_1_out, in_7);
  or or_5 (or_5_out, out_16, demultiplexer_2_out0);
  Demultiplexer #(.enable("false")) demultiplexer_3 (
    .out0(demultiplexer_3_out0), .out1(demultiplexer_3_out1), .in(or_6_out), .sel(RAM));
  or or_6 (or_6_out, RAM, Stack);
  or or_7 (or_7_out, demultiplexer_4_out0, out_28);
  D_Flip_Flop End (.clk(in_3), .D(or_5_out), .Q(out_16), .reset(in_7));  // open: Qn, preset, en
  D_Flip_Flop u_stack (.clk(in_3), .D(demultiplexer_3_out0), .Q(stack_q), .reset(in_7));  // open: Qn, preset, en
  Demultiplexer #(.enable("false")) demultiplexer_4 (.out0(demultiplexer_4_out0), .out1(out_11), .in(CS_0), .sel(Wait));
  D_Flip_Flop u_Wait (.clk(in_3), .D(or_7_out), .Q(CS_0), .reset(in_7));  // open: Qn, preset, en
  or or_8 (out_15, stack_q, demultiplexer_3_out1);
  D_Flip_Flop Save_Instruction (.clk(in_3), .D(out_11), .Q(Save_Instruction_q), .reset(in_7));  // open: Qn, preset, en
  Demultiplexer #(.select(3), .enable("false")) demultiplexer_5 (
    .out0(Brach), .out1(ALU), .out2(Inmediate), .out3(R_W_3), .out4(RAM), .out5(Stack), .out6(Especial),
    .in(Save_Instruction_q), .sel(CU_Op));  // open: out7
  Comparator #(.width(2)) comparator_4 (.a(Especial_Op), .b(2'b11), .eq(comparator_4_eq));  // open: gt, lt
  Demultiplexer #(.enable("false")) demultiplexer_6 (
    .out0(clok_1), .out1(demultiplexer_6_out1), .in(cache_q), .sel(in_4));
  D_Flip_Flop cache (.clk(in_3), .D(out_15), .Q(cache_q), .reset(in_7));  // open: Qn, preset, en
  and and_3 (Salidas, comparator_4_eq, out_21);
  or or_9 (or_9_out, demultiplexer_7_out0, clok_1);
  D_Flip_Flop Read_RAM (.clk(in_3), .D(or_9_out), .Q(CS_1), .reset(in_7));  // open: Qn, preset, en
  or or_10 (or_10_out, demultiplexer_7_out1, demultiplexer_6_out1);
  Demultiplexer #(.enable("false")) demultiplexer_7 (
    .out0(demultiplexer_7_out0), .out1(demultiplexer_7_out1), .in(CS_1), .sel(Wait));
  and and_4 (and_4_out, or_10_out, lw);
  and and_5 (and_5_out, or_10_out, out_17);
  or or_11 (R_W_4, and_4_out, and_5_out);
  or or_12 (out_13, out_15, out_8, CS_1, clok_1, or_10_out);
  D_Flip_Flop Next (.clk(in_3), .D(or_10_out), .Q(out_8), .reset(in_7));  // open: Qn, preset, en
  and and_6 (Write_RAM, CS_1, out_18);
  or or_13 (NORAM, Inmediate, R_W_3, Brach, ALU, TTY, out_10, R_W_6);
  or or_14 (out_21, NORAM, out_8);

  // Other names for the same wires on the sheet: ALU_Op[3:0] = out_9; Branch_Op[2:0] = out_26; clk = in_3;
  //   CS = out_29; E_Cache = out_15; End = out_16; End_RAM = out_8; Func_Code[5:0] = in_5; Hit = in_4;
  //   Load_Inst = out_11; Load_PC = out_21; Logic_I = out_23; Op_Code[5:0] = in_1; pop = out_17; push = out_19;
  //   Push_I = out_13; R_W = out_30; R_W_1 = ALU; R_W_2 = Inmediate; KDP_Enable = out_10; R_W_5 = out_10;
  //   Read = out_22; Read_Time[3:0] = in_2; Register = R_W_3; Reset = in_7; reset_I = out_28; rt_rd = out_24;
  //   Select_Adress[1:0] = out_25; Select_B[1:0] = out_27; Select_DI[2:0] = out_12; TTY_Enable = Salidas;
  //   Write = out_18; Write_Time[3:0] = in_6

  // Notes on the sheet:
  //   Entradas
  //   Type Intruction Selector
endmodule

module Operation_Decoder (
  input  [5:0] Entradas,
  input  [5:0] in_2,
  output out_3,
  output out_4,
  output Salidas,
  output out_6,
  output out_7,
  output out_8,
  output [1:0] out_9,
  output [2:0] out_10,
  output [3:0] out_11,
  output [2:0] out_12,
  output [2:0] out_13,
  output out_14,
  output [1:0] out_15
);

  wire add, addi, ALU, \and , and_6_out, and_7_out, and_8_out, and_9_out, and_10_out, and_11_out, and_22_out,
       and_23_out, and_24_out, and_25_out, and_26_out, and_27_out, and_36_out, and_37_out, and_38_out,
       and_39_out, and_40_out, and_51_out, and_52_out, and_53_out, and_54_out, and_55_out, andi, beq, bgtz,
       blez, bltz, bne, Brach, Cond_Jump, div, divu, Especial, Func_000000, halt, Inmediate, j, jr, kbd,
       mfhi, mflo, mult, Mult_Div, mulu, nop, \nor , Op_000000, Op_111000, Op_111111, \or , or_1_out,
       or_5_out, or_6_out, or_11_out, or_12_out, or_13_out, or_14_out, or_15_out, or_18_out, or_20_out, ori,
       priority_encoder_2_gs, RAM, Register, rnd, slt, slti, sltiu, sltu, Stack, sub, sw, tty, \xor , xori;

  and and_1 (Op_000000, ~Entradas[0], ~Entradas[1], ~Entradas[2], ~Entradas[3], ~Entradas[4], ~Entradas[5]);  // AND_Gate
  and and_2 (Func_000000, ~in_2[0], ~in_2[1], ~in_2[2], ~in_2[3], ~in_2[4], ~in_2[5]);  // AND_Gate
  and and_3 (Op_111000, ~Entradas[0], ~Entradas[1], ~Entradas[2], Entradas[3], Entradas[4], Entradas[5]);  // AND_Gate
  and and_4 (Op_111111, Entradas[0], Entradas[1], Entradas[2], Entradas[3], Entradas[4], Entradas[5]);
  and and_5 (j, ~Entradas[0], Entradas[1], ~Entradas[2], ~Entradas[3], ~Entradas[4], ~Entradas[5]);  // AND_Gate
  or or_1 (or_1_out, 1'b1, halt);
  and and_6 (and_6_out, ~in_2[0], ~in_2[1], ~in_2[2], ~in_2[3], ~in_2[4], in_2[5]);  // AND_Gate
  and and_7 (and_7_out, ~in_2[0], in_2[1], ~in_2[2], ~in_2[3], ~in_2[4], in_2[5]);  // AND_Gate
  and and_8 (and_8_out, ~in_2[0], ~in_2[1], ~in_2[2], in_2[3], in_2[4], ~in_2[5]);  // AND_Gate
  and and_9 (and_9_out, in_2[0], ~in_2[1], ~in_2[2], in_2[3], in_2[4], ~in_2[5]);  // AND_Gate
  and and_10 (and_10_out, ~in_2[0], in_2[1], ~in_2[2], in_2[3], in_2[4], ~in_2[5]);  // AND_Gate
  and and_11 (and_11_out, in_2[0], in_2[1], ~in_2[2], in_2[3], in_2[4], ~in_2[5]);  // AND_Gate
  and and_12 (addi, ~Entradas[0], ~Entradas[1], ~Entradas[2], Entradas[3], ~Entradas[4], ~Entradas[5]);  // AND_Gate
  and and_13 (andi, ~Entradas[0], ~Entradas[1], Entradas[2], Entradas[3], ~Entradas[4], ~Entradas[5]);  // AND_Gate
  Priority_Encoder #(.select(2), .disabled(0)) priority_encoder_1 (
    .in0(or_1_out), .in1(rnd), .in2(kbd), .in3(tty), .out(out_15), .en_in(1'b1));  // open: gs, en_out
  Priority_Encoder #(.disabled(0)) priority_encoder_2 (
    .in0(1'b1), .in1(beq), .in2(bne), .in3(blez), .in4(bgtz), .in5(bltz), .in6(j), .in7(jr), .out(out_13),
    .en_in(1'b1), .gs(priority_encoder_2_gs));  // open: en_out
  and and_14 (add, Op_000000, and_6_out);
  and and_15 (sub, Op_000000, and_7_out);
  and and_16 (mult, Op_000000, and_8_out);
  and and_17 (mulu, Op_000000, and_9_out);
  and and_18 (div, Op_000000, and_10_out);
  and and_19 (divu, Op_000000, and_11_out);
  or or_2 (ALU, add, mulu, mult, \or , slt, \nor , div, \xor , sltu, \and , divu, sub);
  Priority_Encoder #(.disabled(0)) priority_encoder_3 (
    .in0(1'b1), .in1(out_4), .in2(mfhi), .in3(mflo), .in4(kbd), .in5(rnd), .out(out_12), .en_in(1'b1));  // open: in6, in7, gs, en_out
  and and_20 (ori, Entradas[0], ~Entradas[1], Entradas[2], Entradas[3], ~Entradas[4], ~Entradas[5]);  // AND_Gate
  and and_21 (xori, ~Entradas[0], Entradas[1], Entradas[2], Entradas[3], ~Entradas[4], ~Entradas[5]);  // AND_Gate
  and and_22 (and_22_out, ~in_2[0], ~in_2[1], in_2[2], ~in_2[3], ~in_2[4], in_2[5]);  // AND_Gate
  and and_23 (and_23_out, in_2[0], ~in_2[1], in_2[2], ~in_2[3], ~in_2[4], in_2[5]);  // AND_Gate
  and and_24 (and_24_out, in_2[0], in_2[1], in_2[2], ~in_2[3], ~in_2[4], in_2[5]);  // AND_Gate
  and and_25 (and_25_out, ~in_2[0], ~in_2[1], ~in_2[2], in_2[3], ~in_2[4], in_2[5]);  // AND_Gate
  and and_26 (and_26_out, ~in_2[0], in_2[1], ~in_2[2], in_2[3], ~in_2[4], in_2[5]);  // AND_Gate
  and and_27 (and_27_out, in_2[0], in_2[1], ~in_2[2], in_2[3], ~in_2[4], in_2[5]);  // AND_Gate
  Priority_Encoder #(.disabled(0)) priority_encoder_4 (
    .in0(Brach), .in1(ALU), .in2(Inmediate), .in3(Register), .in4(RAM), .in5(Stack), .in6(Especial),
    .out(out_10), .en_in(1'b1));  // open: in7, gs, en_out
  or or_3 (out_8, Op_111000, Op_000000, Op_111111);
  and and_28 (\and , Op_000000, and_22_out);
  and and_29 (\or , Op_000000, and_23_out);
  and and_30 (\nor , Op_000000, and_24_out);
  and and_31 (\xor , Op_000000, and_25_out);
  and and_32 (slt, Op_000000, and_26_out);
  and and_33 (sltu, Op_000000, and_27_out);
  and and_34 (slti, ~Entradas[0], Entradas[1], ~Entradas[2], Entradas[3], ~Entradas[4], ~Entradas[5]);  // AND_Gate
  and and_35 (sltiu, Entradas[0], Entradas[1], ~Entradas[2], Entradas[3], ~Entradas[4], ~Entradas[5]);  // AND_Gate
  or or_4 (Brach, bne, bgtz, blez, j, jr, nop, beq, bltz);
  or or_5 (or_5_out, bgtz, blez, bltz);
  or or_6 (or_6_out, Inmediate, RAM);
  Priority_Encoder #(.select(2), .disabled(0)) priority_encoder_5 (
    .in0(1'b1), .in1(or_5_out), .in2(or_6_out), .out(out_9), .en_in(1'b1));  // open: in3, gs, en_out
  or or_7 (out_4, Salidas, out_6);
  or or_8 (out_7, out_3, sw);
  and and_36 (and_36_out, ~in_2[0], ~in_2[1], ~in_2[2], ~in_2[3], in_2[4], ~in_2[5]);  // AND_Gate
  and and_37 (and_37_out, ~in_2[0], in_2[1], ~in_2[2], ~in_2[3], in_2[4], ~in_2[5]);  // AND_Gate
  and and_38 (and_38_out, ~in_2[0], ~in_2[1], ~in_2[2], in_2[3], ~in_2[4], ~in_2[5]);  // AND_Gate
  and and_39 (and_39_out, ~in_2[0], ~in_2[1], ~in_2[2], ~in_2[3], ~in_2[4], ~in_2[5]);  // AND_Gate
  and and_40 (and_40_out, in_2[0], ~in_2[1], ~in_2[2], ~in_2[3], ~in_2[4], ~in_2[5]);  // AND_Gate
  and and_41 (bne, Entradas[0], ~Entradas[1], Entradas[2], ~Entradas[3], ~Entradas[4], ~Entradas[5]);  // AND_Gate
  and and_42 (blez, ~Entradas[0], Entradas[1], Entradas[2], ~Entradas[3], ~Entradas[4], ~Entradas[5]);  // AND_Gate
  and and_43 (bgtz, Entradas[0], Entradas[1], Entradas[2], ~Entradas[3], ~Entradas[4], ~Entradas[5]);  // AND_Gate
  or or_9 (Cond_Jump, bne, bgtz, beq, blez, bltz);
  and and_44 (mfhi, Op_000000, and_36_out);
  and and_45 (mflo, Op_000000, and_37_out);
  and and_46 (jr, Op_000000, and_38_out);
  and and_47 (Salidas, Op_111000, and_39_out);
  and and_48 (out_3, Op_111000, and_40_out);
  and and_49 (beq, ~Entradas[0], ~Entradas[1], Entradas[2], ~Entradas[3], ~Entradas[4], ~Entradas[5]);  // AND_Gate
  and and_50 (bltz, Entradas[0], ~Entradas[1], ~Entradas[2], ~Entradas[3], ~Entradas[4], ~Entradas[5]);  // AND_Gate
  or or_10 (Inmediate, addi, xori, ori, slti, sltiu, andi);
  or or_11 (or_11_out, RAM, addi, add);
  or or_12 (or_12_out, Cond_Jump, sub);
  or or_13 (or_13_out, \and , andi);
  or or_14 (or_14_out, \or , ori);
  or or_15 (or_15_out, \xor , xori);
  or or_16 (out_14, ori, xori, andi);
  or or_17 (Register, mflo, mfhi);
  or or_18 (or_18_out, slt, slti);
  or or_19 (Stack, Salidas, out_3);
  or or_20 (or_20_out, sltiu, sltu);
  and and_51 (and_51_out, ~ALU, ~Inmediate, ~RAM, ~Cond_Jump);  // AND_Gate
  and and_52 (and_52_out, in_2[0], in_2[1], in_2[2], in_2[3], in_2[4], in_2[5]);
  and and_53 (and_53_out, in_2[0], ~in_2[1], ~in_2[2], ~in_2[3], ~in_2[4], ~in_2[5]);  // AND_Gate
  and and_54 (and_54_out, ~in_2[0], in_2[1], ~in_2[2], ~in_2[3], ~in_2[4], ~in_2[5]);  // AND_Gate
  and and_55 (and_55_out, ~in_2[0], ~in_2[1], in_2[2], ~in_2[3], ~in_2[4], ~in_2[5]);  // AND_Gate
  and and_56 (nop, Op_000000, Func_000000);
  or or_21 (Especial, kbd, rnd, tty, halt);
  or or_22 (RAM, out_6, sw);
  Priority_Encoder #(.select(4), .disabled(0)) priority_encoder_6 (
    .in0(or_11_out), .in1(or_12_out), .in2(or_13_out), .in3(or_14_out), .in4(\nor ), .in5(or_15_out),
    .in6(or_18_out), .in7(or_20_out), .in8(mult), .in9(div), .in10(mulu), .in11(divu), .in15(and_51_out),
    .out(out_11), .en_in(1'b1));  // open: in12, in13, in14, gs, en_out
  and and_57 (halt, Op_111111, and_52_out);
  and and_58 (tty, Op_111111, and_53_out);
  and and_59 (rnd, Op_111111, and_54_out);
  and and_60 (kbd, Op_111111, and_55_out);
  and and_61 (out_6, Entradas[0], Entradas[1], ~Entradas[2], ~Entradas[3], ~Entradas[4], Entradas[5]);  // AND_Gate
  and and_62 (sw, Entradas[0], Entradas[1], ~Entradas[2], Entradas[3], ~Entradas[4], Entradas[5]);  // AND_Gate
  or or_23 (Mult_Div, mult, divu, div, mulu);

  // Other names for the same wires on the sheet: ALU_Op[3:0] = out_11; Branch_Op[2:0] = out_13; CU_Op[2:0] = out_10;
  //   Especial_Op[1:0] = out_15; Func_code[5:0] = in_2; Logical_Inmediate = out_14; lw = out_6;
  //   Op_code[5:0] = Entradas; pop = Salidas; push = out_3; Read_RAM = out_4; rt_rd = out_8; Select_B[1:0] = out_9;
  //   Select_DI[2:0] = out_12; Write_RAM = out_7

  // Notes on the sheet:
  //   Op_Types
  //   Tipo I
  //   Clasificaciones
  //   ALU_Ops
  //   ALU
  //   Register_Ops
  //   Stack_Ops
  //   Branch
  //   Especial_Ops
  //   RAM
endmodule

module Data_Path (
  input  in_1,
  input  in_2,
  input  [2:0] in_3,
  input  in_4,
  input  [1:0] in_5,
  input  [3:0] in_6,
  input  in_7,
  input  [1:0] in_8,
  input  [2:0] in_9,
  input  in_10,
  input  in_11,
  input  in_12,
  input  [31:0] in_13,
  input  in_14,
  input  [6:0] in_15,
  input  in_16,
  input  in_17,
  input  in_18,
  input  in_19,
  input  in_20,
  output [5:0] out_21,
  output [31:0] out_22,
  output [31:0] out_23,
  output [5:0] out_24,
  output [6:0] out_25
);

  wire Hi_Lo_Enable, NF, or_1_out, or_2_out, ZF;
  wire [4:0] Rd, Rs, Rt, SDA;
  wire [15:0] Const;
  wire [25:0] Rute;
  wire [31:0] ALU, bit_extender_1_out, DA, Hi, High, Inst, KBD, KBD_t, Lo, Low, Offset, PC, PC_prime,
       Rand_Generator, RT__prime, RT_t, Sp;
  wire [31:7] RS_t;

  Program_Counter program_counter_1 (.in_1(PC_prime), .in_2(in_20), .in_3(in_17), .in_4(in_12), .out_5(PC));
  Branch_Control branch_control_1 (
    .in_1(PC), .in_2(Rute), .in_3(Offset), .in_4(in_9), .in_5({RS_t, out_25}), .out_8(PC_prime), .in_6(ZF),
    .in_7(NF));
  assign bit_extender_1_out = {{25{1'b0}}, in_15};  // Bit_Extender bit_extender_1
  Random #(.width(32)) random_1 (.clk(in_20), .next(in_20), .out(Rand_Generator));  // open: clr
  Multiplexer #(.width(32), .enable("false")) multiplexer_1 (
    .in0({32{1'b1}}), .in1(bit_extender_1_out), .out(KBD), .sel(in_16));
  Intruction_Decoder intruction_decoder_1 (
    .out_2(out_21), .out_3(Rs), .out_4(Rt), .out_5(Rute), .out_6(Rd), .out_7(Const), .out_8(out_24),
    .in_1(Inst));
  Register #(.width(32)) register_1 (.D(in_13), .en(in_14), .Q(Inst), .clk(in_20), .clr(or_1_out));
  or or_1 (or_1_out, in_7, in_17);
  Register_File register_file_1 (
    .in_1(DA), .in_2(Rs), .in_3(Rt), .in_4(SDA), .in_5(in_20), .in_7(in_1), .in_9(in_17),
    .out_12({RS_t, out_25}), .out_13(RT_t), .out_14(Sp), .in_6(in_19), .in_8(in_18), .in_10(in_10),
    .in_11(in_11));
  Multiplexer #(.width(5), .enable("false")) multiplexer_2 (.in0(Rt), .in1(Rd), .out(SDA), .sel(in_2));
  Multiplexer #(.select(3), .width(32), .enable("false")) multiplexer_3 (
    .in0(ALU), .in1(in_13), .in2(High), .in3(Low), .in4(KBD_t), .in5(Rand_Generator), .out(DA), .sel(in_3));  // open: in6, in7
  Sign_Extender sign_extender_1 (.in_1(Const), .in_2(in_4), .out_3(Offset));
  Multiplexer #(.select(2), .width(32), .enable("false")) multiplexer_4 (
    .in0(RT_t), .in1({32{1'b0}}), .in2(Offset), .out(RT__prime), .sel(in_8));  // open: in3
  ALU alu_1 (
    .in_1({RS_t, out_25}), .in_2(RT__prime), .in_3(in_6), .out_4(ALU), .out_5(Hi), .out_6(Lo), .out_7(ZF),
    .out_8(NF));
  and and_1 (Hi_Lo_Enable, in_6[3], ~in_6[2]);  // AND_Gate
  Register #(.width(32)) register_2 (.D(Hi), .en(Hi_Lo_Enable), .Q(High), .clk(in_20), .clr(in_17));
  Register #(.width(32)) register_3 (.D(Lo), .en(Hi_Lo_Enable), .Q(Low), .clk(in_20), .clr(in_17));
  Multiplexer #(.width(32), .enable("false")) multiplexer_5 (
    .in0(RT_t), .in1({RS_t, out_25}), .out(out_23), .sel(or_2_out));
  or or_2 (or_2_out, in_18, in_19);
  Multiplexer #(.select(2), .width(32)) multiplexer_6 (
    .in0(PC), .in1(ALU), .in2(Sp), .out(out_22), .sel(in_5));  // open: in3, en

  // Other names for the same wires on the sheet: Adress[31:0] = out_22; Adress_Select[1:0] = in_5;
  //   ALU_Select[3:0] = in_6; ALU_Select_B[1:0] = in_8; BS[2:0] = in_9; clk = in_20; DA_Select = in_2;
  //   Data_Select[2:0] = in_3; Enable_Inst = in_14; Enable_PC = in_12; End_RAM = in_11; Func_Code[5:0] = out_24;
  //   KBD_Avalible = in_16; KBD_Data[6:0] = in_15; Op_Code[5:0] = out_21; pop = in_18; push = in_19; push_I = in_10;
  //   R_W = in_1; RAM_DATA[31:0] = in_13; Reset = in_17; Reset_I = in_7; RS_t[6:0] = out_25; TTY_DATA[6:0] = out_25;
  //   SE_Select = in_4; Value[31:0] = out_23

  // Notes on the sheet:
  //   Entradas
  //   DATA PATH
  //   COMPONENTES
  //   COMPLEMENTOS
  //   Salidas
endmodule

module Program_Counter (
  input  [31:0] in_1,
  input  in_2,
  input  in_3,
  input  in_4,
  output [31:0] out_5
);

  wire and_1_out;

  Register #(.width(32)) register_1 (.D(in_1), .en(and_1_out), .Q(out_5), .clk(in_2), .clr(in_3));
  and and_1 (and_1_out, in_4, ~in_3);  // AND_Gate

  // Other names for the same wires on the sheet: clk = in_2; Data[31:0] = in_1; Enable = in_4; Reset = in_3

  // Notes on the sheet:
  //   PC
endmodule

module Branch_Control (
  input  [31:0] in_1,
  input  [25:0] in_2,
  input  [31:0] in_3,
  input  [2:0] in_4,
  input  [31:0] in_5,
  input  in_6,
  input  in_7,
  output [31:0] out_8
);

  wire and_1_out, and_2_out, and_3_out, and_4_out, and_5_out, beq, bgtz, blez, bltz, bne, brach_Jump, j, jr,
       nop, Rs____0;
  wire [1:0] S_Jump;
  wire [31:0] multiplier_1_out, PC___4, PC___4___4___Offset;

  Decoder #(.select(3), .enable("false")) decoder_1 (
    .out0(nop), .out1(beq), .out2(bne), .out3(blez), .out4(bgtz), .out5(bltz), .out6(j), .out7(jr), .sel(in_4));
  and and_1 (and_1_out, beq, in_6);
  and and_2 (and_2_out, bne, ~in_6);  // AND_Gate
  and and_3 (and_3_out, blez, Rs____0);
  and and_4 (and_4_out, bgtz, ~Rs____0);  // AND_Gate
  and and_5 (and_5_out, bltz, in_7);
  Adder #(.width(32)) adder_1 (.a(in_1), .b(32'h4), .out(PC___4));  // open: cin, cout
  Multiplier #(.width(32)) multiplier_1 (.a(in_3), .b(32'h4), .out(multiplier_1_out));  // open: cin, cout
  Adder #(.width(32)) adder_2 (.a(PC___4), .b(multiplier_1_out), .out(PC___4___4___Offset));  // open: cin, cout
  or or_1 (Rs____0, in_6, in_7);
  or or_2 (brach_Jump, and_1_out, and_2_out, and_3_out, and_4_out, and_5_out);
  Priority_Encoder #(.select(2)) priority_encoder_1 (
    .in0(1'b1), .in1(brach_Jump), .in2(j), .in3(jr), .out(S_Jump), .en_in(1'b1));  // open: gs, en_out
  Multiplexer #(.select(2), .width(32), .enable("false")) multiplexer_1 (
    .in0(PC___4), .in1(PC___4___4___Offset), .in2({in_1[3:0], in_2, 2'b00}), .in3(in_5), .out(out_8),
    .sel(S_Jump));

  // Other names for the same wires on the sheet: B_Selector[2:0] = in_4; Jump[31:2] = {in_1[3:0], in_2};
  //   Rute[25:0] = in_2; PC[31:0] = in_1; NF = in_7; Offset[31:0] = in_3; PC_prime[31:0] = out_8; RS[31:0] = in_5;
  //   ZF = in_6

  // Notes on the sheet:
  //   Branch Control
endmodule

module Intruction_Decoder (
  input  [31:0] in_1,
  output [5:0] out_2,
  output [4:0] out_3,
  output [4:0] out_4,
  output [25:0] out_5,
  output [4:0] out_6,
  output [15:0] out_7,
  output [5:0] out_8
);


  assign out_2 = in_1[31:26];
  assign out_3 = in_1[25:21];
  assign out_4 = in_1[20:16];
  assign out_5 = in_1[25:0];
  assign out_6 = in_1[15:11];
  assign out_7 = in_1[15:0];
  assign out_8 = in_1[5:0];

  // Other names for the same wires on the sheet: Constant[15:0] = in_1[15:0]; Func_Code[5:0] = in_1[5:0];
  //   Intruction[31:0] = in_1; Jump_Rute[25:0] = in_1[25:0]; Rd[4:0] = in_1[15:11]; Rt[4:0] = in_1[20:16];
  //   Rs[4:0] = in_1[25:21]; Op_Code[5:0] = in_1[31:26]

  // Notes on the sheet:
  //   Intruction Decoder
endmodule

module Register_File (
  input  [31:0] in_1,
  input  [4:0] in_2,
  input  [4:0] in_3,
  input  [4:0] in_4,
  input  in_5,
  input  in_6,
  input  in_7,
  input  in_8,
  input  in_9,
  input  in_10,
  input  in_11,
  output [31:0] out_12,
  output [31:0] out_13,
  output [31:0] out_14
);

  wire and_1_out, and_2_out, demultiplexer_1_out0, Enable_1, Enable_2, Enable_3, Enable_4, Enable_5,
       Enable_6, Enable_7, Enable_8, Enable_9, Enable_10, Enable_11, Enable_12, Enable_13, Enable_14,
       Enable_15, Enable_16, Enable_17, Enable_18, Enable_19, Enable_20, Enable_21, Enable_22, Enable_23,
       Enable_24, Enable_25, Enable_26, Enable_27, Enable_28, Enable_29, Enable_30, Enable_31, or_1_out;
  wire [31:0] adder_1_out, multiplexer_3_out, multiplexer_4_out, multiplexer_5_out, R0, R1, R2, R3, R4, R5,
       R6, R7, R8, R9, R10, R11, R12, R13, R14, R15, R16, R17, R18, R19, R20, R21, R22, R23, R24, R25, R26,
       R27, R28, R29, R30, subtractor_1_out;

  Multiplexer #(.select(5), .width(32)) multiplexer_1 (
    .in0(R0), .in1(R1), .in2(R2), .in3(R3), .in4(R4), .in5(R5), .in6(R6), .in7(R7), .in8(R8), .in9(R9),
    .in10(R10), .in11(R11), .in12(R12), .in13(R13), .in14(R14), .in15(R15), .in16(R16), .in18(R18),
    .in19(R19), .in20(R20), .in21(R21), .in22(R22), .in23(R23), .in24(R24), .in25(R25), .in26(R26),
    .in27(R27), .in28(R28), .in29(R29), .in30(R30), .in31(out_14), .out(out_12), .sel(in_2));  // open: in17, en
  Demultiplexer #(.select(5)) demultiplexer_1 (
    .out0(demultiplexer_1_out0), .out1(Enable_1), .out2(Enable_2), .out3(Enable_3), .out4(Enable_4),
    .out5(Enable_5), .out6(Enable_6), .out7(Enable_7), .out8(Enable_8), .out9(Enable_9), .out10(Enable_10),
    .out11(Enable_11), .out12(Enable_12), .out13(Enable_13), .out14(Enable_14), .out15(Enable_15),
    .out16(Enable_16), .out17(Enable_17), .out18(Enable_18), .out19(Enable_19), .out20(Enable_20),
    .out21(Enable_21), .out22(Enable_22), .out23(Enable_23), .out24(Enable_24), .out25(Enable_25),
    .out26(Enable_26), .out27(Enable_27), .out28(Enable_28), .out29(Enable_29), .out30(Enable_30),
    .out31(Enable_31), .in(in_7), .sel(in_4));  // open: en
  Multiplexer #(.select(5), .width(32)) multiplexer_2 (
    .in0(R0), .in1(R1), .in2(R2), .in3(R3), .in4(R4), .in5(R5), .in6(R6), .in7(R7), .in8(R8), .in9(R9),
    .in10(R10), .in11(R11), .in12(R12), .in13(R13), .in14(R14), .in15(R15), .in16(R16), .in18(R18),
    .in19(R19), .in20(R20), .in21(R21), .in22(R22), .in23(R23), .in24(R24), .in25(R25), .in26(R26),
    .in27(R27), .in28(R28), .in29(R29), .in30(R30), .in31(out_14), .out(out_13), .sel(in_3));  // open: in17, en
  Register #(.width(32)) register_1 (.D({32{1'b0}}), .Q(R0), .clk(in_5), .clr(in_9));  // open: en
  Register #(.width(32)) register_2 (.D(in_1), .en(Enable_1), .Q(R1), .clk(in_5), .clr(in_9));
  Register #(.width(32)) register_3 (.D(in_1), .en(Enable_2), .Q(R2), .clk(in_5), .clr(in_9));
  Register #(.width(32)) register_4 (.D(in_1), .en(Enable_3), .Q(R3), .clk(in_5), .clr(in_9));
  Register #(.width(32)) register_5 (.D(in_1), .en(Enable_4), .Q(R4), .clk(in_5), .clr(in_9));
  Register #(.width(32)) register_6 (.D(in_1), .en(Enable_5), .Q(R5), .clk(in_5), .clr(in_9));
  Register #(.width(32)) register_7 (.D(in_1), .en(Enable_6), .Q(R6), .clk(in_5), .clr(in_9));
  Register #(.width(32)) register_8 (.D(in_1), .en(Enable_7), .Q(R7), .clk(in_5), .clr(in_9));
  Register #(.width(32)) register_9 (.D(in_1), .en(Enable_8), .Q(R8), .clk(in_5), .clr(in_9));
  Register #(.width(32)) register_10 (.D(in_1), .en(Enable_9), .Q(R9), .clk(in_5), .clr(in_9));
  Register #(.width(32)) register_11 (.D(in_1), .en(Enable_10), .Q(R10), .clk(in_5), .clr(in_9));
  Register #(.width(32)) register_12 (.D(in_1), .en(Enable_11), .Q(R11), .clk(in_5), .clr(in_9));
  Register #(.width(32)) register_13 (.D(in_1), .en(Enable_12), .Q(R12), .clk(in_5), .clr(in_9));
  Register #(.width(32)) register_14 (.D(in_1), .en(Enable_13), .Q(R13), .clk(in_5), .clr(in_9));
  Register #(.width(32)) register_15 (.D(in_1), .en(Enable_14), .Q(R14), .clk(in_5), .clr(in_9));
  Register #(.width(32)) register_16 (.D(in_1), .en(Enable_15), .Q(R15), .clk(in_5), .clr(in_9));
  Register #(.width(32)) register_17 (.D(in_1), .en(Enable_16), .Q(R16), .clk(in_5), .clr(in_9));
  Register #(.width(32)) register_18 (.D(in_1), .en(Enable_17), .Q(R17), .clk(in_5), .clr(in_9));
  Register #(.width(32)) register_19 (.D(in_1), .en(Enable_18), .Q(R18), .clk(in_5), .clr(in_9));
  Register #(.width(32)) register_20 (.D(in_1), .en(Enable_19), .Q(R19), .clk(in_5), .clr(in_9));
  Register #(.width(32)) register_21 (.D(in_1), .en(Enable_20), .Q(R20), .clk(in_5), .clr(in_9));
  Register #(.width(32)) register_22 (.D(in_1), .en(Enable_21), .Q(R21), .clk(in_5), .clr(in_9));
  Register #(.width(32)) register_23 (.D(in_1), .en(Enable_22), .Q(R22), .clk(in_5), .clr(in_9));
  Register #(.width(32)) register_24 (.D(in_1), .en(Enable_23), .Q(R23), .clk(in_5), .clr(in_9));
  Register #(.width(32)) register_25 (.D(in_1), .en(Enable_24), .Q(R24), .clk(in_5), .clr(in_9));
  Register #(.width(32)) register_26 (.D(in_1), .en(Enable_25), .Q(R25), .clk(in_5), .clr(in_9));
  Register #(.width(32)) register_27 (.D(in_1), .en(Enable_26), .Q(R26), .clk(in_5), .clr(in_9));
  Register #(.width(32)) register_28 (.D(in_1), .en(Enable_27), .Q(R27), .clk(in_5), .clr(in_9));
  Register #(.width(32)) register_29 (.D(in_1), .en(Enable_28), .Q(R28), .clk(in_5), .clr(in_9));
  Register #(.width(32)) register_30 (.D(in_1), .en(Enable_29), .Q(R29), .clk(in_5), .clr(in_9));
  Register #(.width(32)) register_31 (.D(in_1), .en(Enable_30), .Q(R30), .clk(in_5), .clr(in_9));
  and and_1 (and_1_out, in_11, in_8);
  Adder #(.width(32)) adder_1 (.a(out_14), .b(32'h4), .out(adder_1_out));  // open: cin, cout
  Multiplexer #(.width(32), .enable("false")) multiplexer_3 (
    .in0(multiplexer_4_out), .in1(in_1), .out(multiplexer_3_out), .sel(Enable_31));
  or or_1 (or_1_out, in_8, in_6, Enable_31);
  Multiplexer #(.width(32), .enable("false")) multiplexer_4 (
    .in0(multiplexer_5_out), .in1(adder_1_out), .out(multiplexer_4_out), .sel(and_1_out));
  Register #(.width(32)) register_32 (.D(multiplexer_3_out), .en(or_1_out), .Q(out_14), .clk(in_5), .clr(in_9));
  Subtractor #(.width(32)) subtractor_1 (.a(out_14), .b(32'h4), .out(subtractor_1_out));  // open: bin, bout
  Multiplexer #(.width(32), .enable("false")) multiplexer_5 (
    .in0(out_14), .in1(subtractor_1_out), .out(multiplexer_5_out), .sel(and_2_out));
  and and_2 (and_2_out, ~in_10, in_6);  // AND_Gate

  // Other names for the same wires on the sheet: A[31:0] = out_12; B[31:0] = out_13; clk = in_5; Data[31:0] = in_1;
  //   End_RAM = in_11; pop = in_8; push = in_6; Push_I = in_10; R_W = in_7; Reset = in_9; Selector_A[4:0] = in_2;
  //   Selector_B[4:0] = in_3; Selector_Data[4:0] = in_4; R31[31:0] = out_14; SP[31:0] = out_14

  // Notes on the sheet:
  //   Entradas
  //   A Selector
  //   B Selector
  //   Data Selector
  //   Registros
  //   Salidas
endmodule

module ALU (
  input  [31:0] in_1,
  input  [31:0] in_2,
  input  [3:0] in_3,
  output [31:0] out_4,
  output [31:0] out_5,
  output [31:0] out_6,
  output out_7,
  output out_8
);

  wire comparator_1_lt, comparator_2_lt;
  wire [31:0] add, \and , Div, Divr, Divu, Divur, Mult, Multr, Mulu, Mulur, \nor , \or , slt, sltu, sub,
       \xor ;

  Mult_Signed mult_signed_1 (.in_1(in_1), .in_2(in_2), .out_3(Mult), .out_4(Multr));
  Multiplier #(.width(32)) multiplier_1 (.a(in_1), .b(in_2), .out(Mulu), .cout(Mulur));  // open: cin
  Divider #(.width(32)) divider_1 (.a(in_1), .b(in_2), .out(Divu), .rem(Divur));  // open: upper
  Div_Signed div_signed_1 (.in_1(in_1), .out_3(Div), .in_2(in_2), .out_4(Divr));
  Adder #(.width(32)) adder_1 (.a(in_1), .b(in_2), .out(add));  // open: cin, cout
  Subtractor #(.width(32)) subtractor_1 (.a(in_1), .b(in_2), .out(sub));  // open: bin, bout
  assign \and  = in_1 & in_2;  // AND_Gate and_1, 32 bits wide
  assign \or  = in_1 | in_2;  // OR_Gate or_1, 32 bits wide
  assign \nor  = ~(in_1 | in_2);  // NOR_Gate nor_1, 32 bits wide
  assign \xor  = in_1 ^ in_2;  // XOR_Gate xor_1, 32 bits wide
  Comparator #(.width(32)) comparator_1 (.a(in_1), .b(in_2), .lt(comparator_1_lt));  // open: gt, eq
  Comparator #(.width(32), .mode("unsigned")) comparator_2 (.a(in_1), .b(in_2), .lt(comparator_2_lt));  // open: gt, eq
  assign slt = {{31{1'b0}}, comparator_1_lt};  // Bit_Extender bit_extender_1
  assign sltu = {{31{1'b0}}, comparator_2_lt};  // Bit_Extender bit_extender_2
  Comparator #(.width(32)) comparator_3 (.a({32{1'b0}}), .b(out_4), .eq(out_7));  // open: gt, lt
  Multiplexer #(.select(2), .width(32)) multiplexer_1 (
    .in0(Multr), .in1(Divr), .in2(Mulur), .in3(Divur), .out(out_5), .sel(in_3[1:0]));  // open: en
  Multiplexer #(.select(2), .width(32)) multiplexer_2 (
    .in0(Mult), .in1(Div), .in2(Mulu), .in3(Divu), .out(out_6), .sel(in_3[1:0]));  // open: en
  Multiplexer #(.select(3), .width(32)) multiplexer_3 (
    .in0(add), .in1(sub), .in2(\and ), .in3(\or ), .in4(\nor ), .in5(\xor ), .in6(slt), .in7(sltu),
    .out(out_4), .sel(in_3[2:0]));  // open: en

  assign out_8 = out_4[31];

  // Other names for the same wires on the sheet: Hi[31:0] = out_5; Lo[31:0] = out_6; Rd[31:0] = out_4; NF = out_4[31];
  //   Rs[31:0] = in_1; Rt[31:0] = in_2; Selector[2:0] = in_3[2:0]; Selector_ALU[3:0] = in_3;
  //   Selector_Hi_Lo[1:0] = in_3[1:0]; ZF = out_7

  // Notes on the sheet:
  //   Entradas
  //   ALU
  //   Salidas
endmodule

module Mult_Signed (
  input  [31:0] in_1,
  input  [31:0] in_2,
  output [31:0] out_3,
  output [31:0] out_4
);

  wire A_2_31, adder_3_cout, adder_4_cout, B_2_31, comparator_1_eq, comparator_2_eq, Especial, Especial_A,
       Especial_B;
  wire [30:0] Carry_Especial;
  wire [31:0] _00_Carry, _00_Rd, _01_Carry, _01_Rd, _10_Carry, _10_Rd, _11_Carry, _11_Rd, bit_extender_1_out,
       bit_extender_2_out, Carry_Normal, multiplier_3_cout, multiplier_3_out, multiplier_4_cout,
       multiplier_4_out, nA, nand_1_out, nand_2_out, nand_3_out, nand_4_out, nB, Rd_Normal;
  wire [31:31] Mult_Especial;

  Negator #(.width(32)) negator_1 (.in(in_1), .out(nA));
  Negator #(.width(32)) negator_2 (.in(in_2), .out(nB));
  Multiplier #(.width(32)) multiplier_1 (.a(in_1), .b(in_2), .out(_00_Rd), .cout(_00_Carry));  // open: cin
  Comparator #(.width(31)) comparator_1 (.a(in_1[30:0]), .b({31{1'b0}}), .eq(comparator_1_eq));  // open: gt, lt
  Comparator #(.width(31)) comparator_2 (.a(in_2[30:0]), .b({31{1'b0}}), .eq(comparator_2_eq));  // open: gt, lt
  Multiplier #(.width(32)) multiplier_2 (.a(nA), .b(nB), .out(_11_Rd), .cout(_11_Carry));  // open: cin
  and and_1 (A_2_31, in_1[31], comparator_1_eq);
  and and_2 (B_2_31, in_2[31], comparator_2_eq);
  Multiplier #(.width(32)) multiplier_3 (
    .a(in_1), .b(nB), .out(multiplier_3_out), .cout(multiplier_3_cout));  // open: cin
  Multiplier #(.width(32)) multiplier_4 (
    .a(nA), .b(in_2), .out(multiplier_4_out), .cout(multiplier_4_cout));  // open: cin
  and and_3 (Especial_A, in_2[31], A_2_31);
  and and_4 (Especial_B, B_2_31, in_1[31]);
  assign nand_1_out = ~(multiplier_3_out & {32{1'b1}});  // NAND_Gate nand_1, 32 bits wide
  assign nand_2_out = ~(multiplier_3_cout & {32{1'b1}});  // NAND_Gate nand_2, 32 bits wide
  assign bit_extender_1_out = {{31{1'b0}}, adder_3_cout};  // Bit_Extender bit_extender_1
  assign nand_3_out = ~(multiplier_4_out & {32{1'b1}});  // NAND_Gate nand_3, 32 bits wide
  assign nand_4_out = ~(multiplier_4_cout & {32{1'b1}});  // NAND_Gate nand_4, 32 bits wide
  assign bit_extender_2_out = {{31{1'b0}}, adder_4_cout};  // Bit_Extender bit_extender_2
  Adder #(.width(32)) adder_1 (.a(nand_2_out), .b(bit_extender_1_out), .out(_01_Carry));  // open: cin, cout
  Adder #(.width(32)) adder_2 (.a(nand_4_out), .b(bit_extender_2_out), .out(_10_Carry));  // open: cin, cout
  or or_1 (Especial, Especial_A, Especial_B);
  Adder #(.width(32)) adder_3 (.a(nand_1_out), .b(32'h1), .out(_01_Rd), .cout(adder_3_cout));  // open: cin
  Adder #(.width(32)) adder_4 (.a(nand_3_out), .b(32'h1), .out(_10_Rd), .cout(adder_4_cout));  // open: cin
  Multiplexer #(.width(32)) multiplexer_1 (
    .in0(nA), .in1(nB), .out({Carry_Especial, Mult_Especial[31]}), .sel(Especial_A));  // open: en
  Multiplexer #(.select(2), .width(32), .enable("false")) multiplexer_2 (
    .in0(_00_Rd), .in1(_01_Rd), .in2(_10_Rd), .in3(_11_Rd), .out(Rd_Normal), .sel({in_1[31], in_2[31]}));
  Multiplexer #(.select(2), .width(32), .enable("false")) multiplexer_3 (
    .in0(_00_Carry), .in1(_01_Carry), .in2(_10_Carry), .in3(_11_Carry), .out(Carry_Normal),
    .sel({in_1[31], in_2[31]}));
  Multiplexer #(.width(32)) multiplexer_4 (
    .in0(Rd_Normal), .in1({Mult_Especial[31], {31{1'b0}}}), .out(out_3), .sel(Especial));  // open: en
  Multiplexer #(.width(32)) multiplexer_5 (
    .in0(Carry_Normal), .in1({1'b0, Carry_Especial}), .out(out_4), .sel(Especial));  // open: en

  // Other names for the same wires on the sheet: B[31:0] = in_2; B_Sign = in_2[31]; A[31:0] = in_1; A_Sign = in_1[31];
  //   A_31[30:0] = in_1[30:0]; B_31[30:0] = in_2[30:0]; Carry[31:0] = out_4;
  //   nChose[31:0] = {Carry_Especial, Mult_Especial[31]}; Rd[31:0] = out_3

  // Notes on the sheet:
  //   Entradas
  //   Especial
  //   Mult Signo
  //   Salidas
endmodule

module Div_Signed (
  input  [31:0] in_1,
  input  [31:0] in_2,
  output [31:0] out_3,
  output [31:0] out_4
);

  wire [31:0] _00, _00_C, _01, _01_C, _10, _10_C, _11, _11_C, divider_1_rem, divider_3_out, divider_4_out,
       divider_4_rem, negator_1_out, negator_2_out, negator_4_out, negator_5_out;

  Negator #(.width(32)) negator_1 (.in(in_1), .out(negator_1_out));
  Negator #(.width(32)) negator_2 (.in(in_2), .out(negator_2_out));
  Divider #(.width(32)) divider_1 (
    .a(negator_1_out), .b(negator_2_out), .out(_11), .rem(divider_1_rem));  // open: upper
  Negator #(.width(32)) negator_3 (.in(divider_1_rem), .out(_11_C));
  Divider #(.width(32)) divider_2 (.a(in_1), .b(in_2), .out(_00), .rem(_00_C));  // open: upper
  Negator #(.width(32)) negator_4 (.in(in_1), .out(negator_4_out));
  Divider #(.width(32)) divider_3 (.a(in_1), .b(negator_5_out), .out(divider_3_out), .rem(_01_C));  // open: upper
  Negator #(.width(32)) negator_5 (.in(in_2), .out(negator_5_out));
  Divider #(.width(32)) divider_4 (
    .a(negator_4_out), .b(in_2), .out(divider_4_out), .rem(divider_4_rem));  // open: upper
  Negator #(.width(32)) negator_6 (.in(divider_4_rem), .out(_10_C));
  Negator #(.width(32)) negator_7 (.in(divider_3_out), .out(_01));
  Negator #(.width(32)) negator_8 (.in(divider_4_out), .out(_10));
  Multiplexer #(.select(2), .width(32), .enable("false")) multiplexer_1 (
    .in0(_00), .in1(_01), .in2(_10), .in3(_11), .out(out_3), .sel({in_1[31], in_2[31]}));
  Multiplexer #(.select(2), .width(32), .enable("false")) multiplexer_2 (
    .in0(_00_C), .in1(_01_C), .in2(_10_C), .in3(_11_C), .out(out_4), .sel({in_1[31], in_2[31]}));

  // Other names for the same wires on the sheet: B[31:0] = in_2; A[31:0] = in_1; BMS_B = in_2[31]; BMS_A = in_1[31];
  //   Carry[31:0] = out_4; Rd[31:0] = out_3

  // Notes on the sheet:
  //   Entradas
  //   Div Signo
  //   Salidas
endmodule

module Sign_Extender (
  input  [15:0] in_1,
  input  in_2,
  output [31:0] out_3
);

  wire [31:0] bit_extender_1_out, bit_extender_2_out;

  assign bit_extender_1_out = {{16{in_1[15]}}, in_1};  // Bit_Extender bit_extender_1
  assign bit_extender_2_out = {{16{1'b0}}, in_1};  // Bit_Extender bit_extender_2
  Multiplexer #(.width(32)) multiplexer_1 (
    .in0(bit_extender_1_out), .in1(bit_extender_2_out), .out(out_3), .sel(in_2));  // open: en

  // Other names for the same wires on the sheet: Input[15:0] = in_1; Output[31:0] = out_3; Sign = in_2

  // Notes on the sheet:
  //   Sign Extender
endmodule

module RAM_Manager (
  input  [31:0] in_1,
  input  [31:0] in_2,
  input  [31:0] in_3,
  input  [31:0] in_4,
  input  in_5,
  input  [31:0] in_6,
  input  [31:0] in_7,
  input  in_8,
  input  in_9,
  output [15:0] out_10,
  output [3:0] Salidas,
  output [31:0] out_12,
  output [1:0] out_13,
  output [31:0] out_14,
  output [31:0] out_15,
  output [31:0] out_16,
  output [31:0] out_17
);

  Decoder #(.select(2), .enable("false")) decoder_1 (
    .out0(Salidas[0]), .out1(Salidas[1]), .out2(Salidas[2]), .out3(Salidas[3]), .sel(in_3[3:2]));
  Multiplexer #(.select(2), .width(32), .enable("false")) multiplexer_1 (
    .in0(in_1), .in1(in_2), .in2(in_6), .in3(in_7),
    .out({out_12[7:0], out_12[15:8], out_12[23:16], out_12[31:24]}), .sel(in_3[3:2]));
  Demultiplexer #(.select(2), .width(32), .enable("false")) demultiplexer_1 (
    .out0(out_14), .out1(out_15), .out2(out_16), .out3(out_17),
    .in({in_4[7:0], in_4[15:8], in_4[23:16], in_4[31:24]}), .sel(in_3[3:2]));

  assign out_10 = in_3[19:4];
  assign out_13 = in_3[3:2];

  // Other names for the same wires on the sheet: Value[31:0] = in_4; Adress_In[31:0] = in_3; Bank[1:0] = in_3[3:2];
  //   Adress_Out[15:0] = in_3[19:4]; clk = in_8; Hit = in_5; Mask[3:0] = Salidas; RAM_INPUT_0[31:0] = out_14;
  //   RAM_INPUT_1[31:0] = out_15; RAM_INPUT_2[31:0] = out_16; RAM_INPUT_3[31:0] = out_17; RAM_Out[31:0] = out_12;
  //   RAM_OUTPUT_0[31:0] = in_1; RAM_OUTPUT_1[31:0] = in_2; RAM_OUTPUT_2[31:0] = in_6; RAM_OUTPUT_3[31:0] = in_7;
  //   Reset = in_9

  // Notes on the sheet:
  //   Entradas
  //   Little Endian - Big Endian
endmodule

module Cache (
  input  in_1,
  input  in_2,
  input  in_3,
  input  [31:0] in_4,
  input  in_5,
  input  in_6,
  input  [31:0] in_7,
  input  [31:0] in_8,
  input  [31:0] in_9,
  input  [31:0] in_10,
  input  [31:0] in_11,
  output out_12,
  output [31:0] out_13,
  output [31:0] out_14
);

  wire and_1_out, Bank_0, Bank_1, Bank_2, Bank_3, Cache_Use, comparator_1_eq, Hit, L0_E, L1_E, L2_E, L3_E;
  wire [14:0] tag_0, tag_1, tag_2, tag_3, tag_select;
  wire [31:0] Bank_00, Bank_01, Bank_02, Bank_03, Bank_10, Bank_11, Bank_12, Bank_13, Bank_20, Bank_21,
       Bank_22, Bank_23, Bank_30, Bank_31, Bank_32, Bank_33, Bank_L0, Bank_L1, Bank_L2, Bank_L3, Read_00,
       Read_01, Read_02, Read_03;

  Multiplexer #(.width(32), .enable("false")) multiplexer_1 (
    .in0({in_8[7:0], in_8[15:8], in_8[23:16], in_8[31:24]}), .in1(in_7), .out(Read_00), .sel(Bank_0));
  Multiplexer #(.width(32), .enable("false")) multiplexer_2 (
    .in0({in_9[7:0], in_9[15:8], in_9[23:16], in_9[31:24]}), .in1(in_7), .out(Read_01), .sel(Bank_1));
  Decoder #(.select(2), .enable("false")) decoder_1 (
    .out0(Bank_0), .out1(Bank_1), .out2(Bank_2), .out3(Bank_3), .sel(in_4[3:2]));
  Multiplexer #(.width(32), .enable("false")) multiplexer_3 (
    .in0({in_10[7:0], in_10[15:8], in_10[23:16], in_10[31:24]}), .in1(in_7), .out(Read_02), .sel(Bank_2));
  Multiplexer #(.width(32), .enable("false")) multiplexer_4 (
    .in0({in_11[7:0], in_11[15:8], in_11[23:16], in_11[31:24]}), .in1(in_7), .out(Read_03), .sel(Bank_3));
  Register #(.width(15)) register_1 (.D({1'b1, in_4[19:6]}), .en(L0_E), .Q(tag_0), .clk(in_1), .clr(in_3));
  Register #(.width(15)) register_2 (.D({1'b1, in_4[19:6]}), .en(L1_E), .Q(tag_1), .clk(in_1), .clr(in_3));
  Register #(.width(15)) register_3 (.D({1'b1, in_4[19:6]}), .en(L2_E), .Q(tag_2), .clk(in_1), .clr(in_3));
  Register #(.width(15)) register_4 (.D({1'b1, in_4[19:6]}), .en(L3_E), .Q(tag_3), .clk(in_1), .clr(in_3));
  or or_1 (Cache_Use, in_5, in_6);
  Multiplexer #(.select(2), .width(15), .enable("false")) multiplexer_5 (
    .in0(tag_0), .in1(tag_1), .in2(tag_2), .in3(tag_3), .out(tag_select), .sel(in_4[5:4]));
  and and_1 (and_1_out, in_6, in_2);
  Demultiplexer #(.select(2), .enable("false")) demultiplexer_1 (
    .out0(L0_E), .out1(L1_E), .out2(L2_E), .out3(L3_E), .in(and_1_out), .sel(in_4[3:2]));
  Comparator #(.width(14)) comparator_1 (.a(tag_select[13:0]), .b(in_4[19:6]), .eq(comparator_1_eq));  // open: gt, lt
  and and_2 (Hit, comparator_1_eq, tag_select[14]);
  Register #(.width(32)) register_5 (.D(Read_00), .en(L0_E), .Q(Bank_00), .clk(in_1), .clr(in_3));
  Register #(.width(32)) register_6 (.D(Read_00), .en(L1_E), .Q(Bank_01), .clk(in_1), .clr(in_3));
  Register #(.width(32)) register_7 (.D(Read_00), .en(L2_E), .Q(Bank_02), .clk(in_1), .clr(in_3));
  Register #(.width(32)) register_8 (.D(Read_00), .en(L3_E), .Q(Bank_03), .clk(in_1), .clr(in_3));
  Multiplexer #(.select(2), .width(32), .enable("false")) multiplexer_6 (
    .in0(Bank_00), .in1(Bank_10), .in2(Bank_20), .in3(Bank_30), .out(Bank_L0), .sel(in_4[3:2]));
  Register #(.width(32)) register_9 (.D(Read_01), .en(L0_E), .Q(Bank_10), .clk(in_1), .clr(in_3));
  Register #(.width(32)) register_10 (.D(Read_01), .en(L1_E), .Q(Bank_11), .clk(in_1), .clr(in_3));
  Register #(.width(32)) register_11 (.D(Read_01), .en(L2_E), .Q(Bank_12), .clk(in_1), .clr(in_3));
  Register #(.width(32)) register_12 (.D(Read_01), .en(L3_E), .Q(Bank_13), .clk(in_1), .clr(in_3));
  Multiplexer #(.select(2), .width(32), .enable("false")) multiplexer_7 (
    .in0(Bank_01), .in1(Bank_11), .in2(Bank_21), .in3(Bank_31), .out(Bank_L1), .sel(in_4[3:2]));
  Register #(.width(32)) register_13 (.D(Read_02), .en(L0_E), .Q(Bank_20), .clk(in_1), .clr(in_3));
  Register #(.width(32)) register_14 (.D(Read_02), .en(L1_E), .Q(Bank_21), .clk(in_1), .clr(in_3));
  Register #(.width(32)) register_15 (.D(Read_02), .en(L2_E), .Q(Bank_22), .clk(in_1), .clr(in_3));
  Register #(.width(32)) register_16 (.D(Read_02), .en(L3_E), .Q(Bank_23), .clk(in_1), .clr(in_3));
  Multiplexer #(.select(2), .width(32), .enable("false")) multiplexer_8 (
    .in0(Bank_02), .in1(Bank_12), .in2(Bank_22), .in3(Bank_32), .out(Bank_L2), .sel(in_4[3:2]));
  Register #(.width(32)) register_17 (.D(Read_03), .en(L0_E), .Q(Bank_30), .clk(in_1), .clr(in_3));
  Register #(.width(32)) register_18 (.D(Read_03), .en(L1_E), .Q(Bank_31), .clk(in_1), .clr(in_3));
  Register #(.width(32)) register_19 (.D(Read_03), .en(L2_E), .Q(Bank_32), .clk(in_1), .clr(in_3));
  Register #(.width(32)) register_20 (.D(Read_03), .en(L3_E), .Q(Bank_33), .clk(in_1), .clr(in_3));
  Multiplexer #(.select(2), .width(32), .enable("false")) multiplexer_9 (
    .in0(Bank_03), .in1(Bank_13), .in2(Bank_23), .in3(Bank_33), .out(Bank_L3), .sel(in_4[3:2]));
  Register #(.width(32)) register_21 (.D(in_7), .en(in_6), .Q(out_14), .clk(in_1), .clr(in_3));
  and and_3 (out_12, Hit, in_5);
  Multiplexer #(.select(2), .width(32), .enable("false")) multiplexer_10 (
    .in0(Bank_L0), .in1(Bank_L1), .in2(Bank_L2), .in3(Bank_L3), .out(out_13), .sel(in_4[5:4]));

  // Other names for the same wires on the sheet: RAM_O1[31:0] = in_9; RAM_O0[31:0] = in_8; RAM_O2[31:0] = in_10;
  //   RAM_O3[31:0] = in_11; adress[31:0] = in_4; tag_In[13:0] = in_4[19:6]; adr[1:0] = in_4[5:4];
  //   Bank[1:0] = in_4[3:2]; Cache_Data[31:0] = out_13; clk = in_1; E_Cache = in_2; Read = in_5; Reset = in_3;
  //   tag_select_Out[13:0] = tag_select[13:0]; valid = tag_select[14]; Value[31:0] = in_7; write = in_6

  // Notes on the sheet:
  //   Entradas
  //   Tag_Data
  //   Banks
  //   Salidas
endmodule
